// Logisim project CPU Design.circ as structural Verilog: 37 circuits, main circuit main
module main (
);

  wire blockbottom_1_out_5, blockbottom_1_out_6, blockbottom_1_out_7, blockbottom_1_out_8,
       blockbottom_1_out_9, blockbottom_1_out_10, blockbottom_1_out_11, blockbottom_1_out_12,
       blockbottom_1_out_13, blockbottom_1_out_14, blockbottom_1_out_15, blockbottom_1_out_16,
       blockbottom_1_out_17, blockbottom_1_out_18, blockbottom_1_out_19, blockbottom_1_out_20,
       blocktop_1_out_5, blocktop_1_out_6, blocktop_1_out_7, blocktop_1_out_8, blocktop_1_out_9,
       blocktop_1_out_10, blocktop_1_out_11, blocktop_1_out_12, blocktop_1_out_13, blocktop_1_out_14,
       blocktop_1_out_15, blocktop_1_out_16, blocktop_1_out_17, blocktop_1_out_18, blocktop_1_out_19,
       blocktop_1_out_20, control_1_alusrc, control_1_disp, control_1_extend, control_1_memtoreg,
       control_1_memwr, control_1_npc_sel, control_1_regdest, control_1_whether_jump,
       control_1_writing_enable, converterbottom_1_out_2, converterbottom_1_out_3, converterbottom_1_out_4,
       converterbottom_1_out_5, converterbottom_2_out_2, converterbottom_2_out_3, converterbottom_2_out_4,
       converterbottom_2_out_5, converterbottom_3_out_2, converterbottom_3_out_3, converterbottom_3_out_4,
       converterbottom_3_out_5, converterbottom_4_out_2, converterbottom_4_out_3, converterbottom_4_out_4,
       converterbottom_4_out_5, convertertop_1_out_2, convertertop_1_out_3, convertertop_1_out_4,
       convertertop_1_out_5, convertertop_2_out_2, convertertop_2_out_3, convertertop_2_out_4,
       convertertop_2_out_5, convertertop_3_out_2, convertertop_3_out_3, convertertop_3_out_4,
       convertertop_3_out_5, convertertop_4_out_2, convertertop_4_out_3, convertertop_4_out_4,
       convertertop_4_out_5;
  wire [2:0] datapath_1_funct;
  wire [3:0] control_1_aluctr, datapath_1_opcode;
  wire [7:0] datapath_1_disp_0, datapath_1_disp_1, datapath_1_disp_2, datapath_1_disp_3, datapath_1_reg0_2,
       datapath_1_reg1_2, datapath_1_reg2_2, undriven;
  wire [15:0] datapath_1_reg0, datapath_1_reg1, datapath_1_reg2;
  wire [15:9] datapath_1_reg3;

  ConverterTop convertertop_1 (
    .in_1(undriven), .out_2(convertertop_1_out_2), .out_3(convertertop_1_out_3),
    .out_4(convertertop_1_out_4), .out_5(convertertop_1_out_5));
  _7_Segment_Display u_7_segment_display_1 (
    .g(convertertop_1_out_2), .f(convertertop_1_out_3), .a(convertertop_1_out_4), .b(convertertop_1_out_5),
    .e(converterbottom_1_out_2), .d(converterbottom_1_out_3), .c(converterbottom_1_out_4),
    .dp(converterbottom_1_out_5));
  ConverterBottom converterbottom_1 (
    .in_1(undriven), .out_2(converterbottom_1_out_2), .out_3(converterbottom_1_out_3),
    .out_4(converterbottom_1_out_4), .out_5(converterbottom_1_out_5));
  ConverterTop convertertop_2 (
    .in_1(datapath_1_reg0_2), .out_2(convertertop_2_out_2), .out_3(convertertop_2_out_3),
    .out_4(convertertop_2_out_4), .out_5(convertertop_2_out_5));
  _7_Segment_Display u_7_segment_display_2 (
    .g(convertertop_2_out_2), .f(convertertop_2_out_3), .a(convertertop_2_out_4), .b(convertertop_2_out_5),
    .e(converterbottom_2_out_2), .d(converterbottom_2_out_3), .c(converterbottom_2_out_4),
    .dp(converterbottom_2_out_5));
  ConverterBottom converterbottom_2 (
    .in_1(datapath_1_reg0_2), .out_2(converterbottom_2_out_2), .out_3(converterbottom_2_out_3),
    .out_4(converterbottom_2_out_4), .out_5(converterbottom_2_out_5));
  ConverterTop convertertop_3 (
    .in_1(datapath_1_reg1_2), .out_2(convertertop_3_out_2), .out_3(convertertop_3_out_3),
    .out_4(convertertop_3_out_4), .out_5(convertertop_3_out_5));
  _7_Segment_Display u_7_segment_display_3 (
    .g(convertertop_3_out_2), .f(convertertop_3_out_3), .a(convertertop_3_out_4), .b(convertertop_3_out_5),
    .e(converterbottom_3_out_2), .d(converterbottom_3_out_3), .c(converterbottom_3_out_4),
    .dp(converterbottom_3_out_5));
  ConverterBottom converterbottom_3 (
    .in_1(datapath_1_reg1_2), .out_2(converterbottom_3_out_2), .out_3(converterbottom_3_out_3),
    .out_4(converterbottom_3_out_4), .out_5(converterbottom_3_out_5));
  ConverterTop convertertop_4 (
    .in_1(datapath_1_reg2_2), .out_2(convertertop_4_out_2), .out_3(convertertop_4_out_3),
    .out_4(convertertop_4_out_4), .out_5(convertertop_4_out_5));
  _7_Segment_Display u_7_segment_display_4 (
    .g(convertertop_4_out_2), .f(convertertop_4_out_3), .a(convertertop_4_out_4), .b(convertertop_4_out_5),
    .e(converterbottom_4_out_2), .d(converterbottom_4_out_3), .c(converterbottom_4_out_4),
    .dp(converterbottom_4_out_5));
  ConverterBottom converterbottom_4 (
    .in_1(datapath_1_reg2_2), .out_2(converterbottom_4_out_2), .out_3(converterbottom_4_out_3),
    .out_4(converterbottom_4_out_4), .out_5(converterbottom_4_out_5));
  Control control_1 (
    .Funct(datapath_1_funct), .Opcode(datapath_1_opcode), .ALUctr(control_1_aluctr),
    .RegDest(control_1_regdest), .Writing_Enable(control_1_writing_enable), .DISP(control_1_disp),
    .ALUsrc(control_1_alusrc), .Extend(control_1_extend), .MemToReg(control_1_memtoreg),
    .MemWR(control_1_memwr), .Whether_Jump(control_1_whether_jump), .nPC_Sel(control_1_npc_sel));
  DATAPATH datapath_1 (
    .REG0({datapath_1_reg0[15], datapath_1_reg0_2, datapath_1_reg0[6:0]}),
    .REG1({datapath_1_reg1[15], datapath_1_reg1_2, datapath_1_reg1[6:0]}),
    .REG2({datapath_1_reg2[15], datapath_1_reg2_2, datapath_1_reg2[6:0]}),
    .REG3({datapath_1_reg3, datapath_1_reg2[15], datapath_1_reg2_2}), .RegDst(control_1_regdest),
    .Funct(datapath_1_funct), .Opcode(datapath_1_opcode), .DISP_3(datapath_1_disp_3),
    .DISP_2(datapath_1_disp_2), .DISP_1(datapath_1_disp_1), .DISP_0(datapath_1_disp_0),
    .DISP(control_1_disp), .in_2(control_1_writing_enable), .Extend(control_1_extend),
    .in_4(control_1_alusrc), .ALUctr(control_1_aluctr), .MemWR(control_1_memwr), .in_7(control_1_memtoreg),
    .nPC_sel(control_1_npc_sel), .Whether_jump(control_1_whether_jump));  // open: Party_bit
  _7_Segment_Display u_7_segment_display_5 (
    .g(blocktop_1_out_5), .f(blocktop_1_out_13), .a(blocktop_1_out_14), .b(blocktop_1_out_6),
    .e(blockbottom_1_out_13), .d(blockbottom_1_out_5), .c(blockbottom_1_out_6), .dp(blockbottom_1_out_14));
  BlockBottom blockbottom_1 (
    .out_13(blockbottom_1_out_13), .out_5(blockbottom_1_out_5), .out_6(blockbottom_1_out_6),
    .out_14(blockbottom_1_out_14), .out_15(blockbottom_1_out_15), .out_7(blockbottom_1_out_7),
    .out_8(blockbottom_1_out_8), .out_16(blockbottom_1_out_16), .out_17(blockbottom_1_out_17),
    .out_9(blockbottom_1_out_9), .out_10(blockbottom_1_out_10), .out_18(blockbottom_1_out_18),
    .out_19(blockbottom_1_out_19), .out_11(blockbottom_1_out_11), .out_12(blockbottom_1_out_12),
    .out_20(blockbottom_1_out_20), .in_1(datapath_1_disp_3), .in_2(datapath_1_disp_2),
    .in_3(datapath_1_disp_1), .in_4(datapath_1_disp_0));
  BlockTop blocktop_1 (
    .in_1(datapath_1_disp_3), .in_2(datapath_1_disp_2), .in_3(datapath_1_disp_1), .in_4(datapath_1_disp_0),
    .out_5(blocktop_1_out_5), .out_13(blocktop_1_out_13), .out_14(blocktop_1_out_14),
    .out_6(blocktop_1_out_6), .out_7(blocktop_1_out_7), .out_15(blocktop_1_out_15),
    .out_16(blocktop_1_out_16), .out_8(blocktop_1_out_8), .out_9(blocktop_1_out_9),
    .out_17(blocktop_1_out_17), .out_18(blocktop_1_out_18), .out_10(blocktop_1_out_10),
    .out_11(blocktop_1_out_11), .out_19(blocktop_1_out_19), .out_20(blocktop_1_out_20),
    .out_12(blocktop_1_out_12));
  _7_Segment_Display u_7_segment_display_6 (
    .g(blocktop_1_out_7), .f(blocktop_1_out_15), .a(blocktop_1_out_16), .b(blocktop_1_out_8),
    .e(blockbottom_1_out_15), .d(blockbottom_1_out_7), .c(blockbottom_1_out_8), .dp(blockbottom_1_out_16));
  _7_Segment_Display u_7_segment_display_7 (
    .g(blocktop_1_out_9), .f(blocktop_1_out_17), .a(blocktop_1_out_18), .b(blocktop_1_out_10),
    .e(blockbottom_1_out_17), .d(blockbottom_1_out_9), .c(blockbottom_1_out_10), .dp(blockbottom_1_out_18));
  _7_Segment_Display u_7_segment_display_8 (
    .g(blocktop_1_out_11), .f(blocktop_1_out_19), .a(blocktop_1_out_20), .b(blocktop_1_out_12),
    .e(blockbottom_1_out_19), .d(blockbottom_1_out_11), .c(blockbottom_1_out_12), .dp(blockbottom_1_out_20));

  // Notes on the sheet:
  //   Reg0
  //   Reg1
  //   Reg2
  //   Reg3
  //   CONTROL
  //   DATAPATH
  //   DISP[3]
  //   DISP[1]
  //   DISP[2]
  //   DISP[2]
  //   DISP[0]
  //   BlockTop
  //   BlockBottom
endmodule

module _1bit_ADDER (
  input  ai,
  input  bi,
  input  ci,
  output ci_1,
  output si
);

  wire and_1_out, and_2_out, and_3_out, xor_1_out_3;

  or or_1 (ci_1, and_1_out, and_2_out, and_3_out);
  and and_1 (and_1_out, ai, bi);
  and and_2 (and_2_out, ai, ci);
  and and_3 (and_3_out, bi, ci);
  XOR xor_1 (.in_1(bi), .in_2(ai), .out_3(xor_1_out_3));
  XOR xor_2 (.in_1(xor_1_out_3), .in_2(ci), .out_3(si));

  // Notes on the sheet:
  //   XOR
  //   XOR
endmodule

module XOR (
  input  in_1,
  input  in_2,
  output out_3
);

  wire and_1_out, and_2_out, not_1_out, not_2_out;

  not not_1 (not_1_out, in_1);
  not not_2 (not_2_out, in_2);
  and and_1 (and_1_out, not_1_out, in_2);
  and and_2 (and_2_out, not_2_out, in_1);
  or or_1 (out_3, and_1_out, and_2_out);
endmodule

module _16bit_ADDER (
  input  [15:0] in_1,
  input  [15:0] in_2,
  input  SUB,
  output Overflow,
  output [15:0] out_5
);

  wire n1bit_adder_1_ci_1, n1bit_adder_2_ci_1, n1bit_adder_3_ci_1, n1bit_adder_4_ci_1, n1bit_adder_5_ci_1,
       n1bit_adder_6_ci_1, n1bit_adder_7_ci_1, n1bit_adder_8_ci_1, n1bit_adder_9_ci_1, n1bit_adder_10_ci_1,
       n1bit_adder_11_ci_1, n1bit_adder_12_ci_1, n1bit_adder_13_ci_1, n1bit_adder_14_ci_1,
       n1bit_adder_15_ci_1, n1bit_adder_16_ci_1, xor_2_out_3, xor_3_out_3, xor_4_out_3, xor_5_out_3,
       xor_6_out_3, xor_7_out_3, xor_8_out_3, xor_9_out_3, xor_10_out_3, xor_11_out_3, xor_12_out_3,
       xor_13_out_3, xor_14_out_3, xor_15_out_3, xor_16_out_3, xor_17_out_3;

  XOR xor_1 (.in_1(n1bit_adder_1_ci_1), .in_2(n1bit_adder_2_ci_1), .out_3(Overflow));
  XOR xor_2 (.in_1(SUB), .in_2(in_1[14]), .out_3(xor_2_out_3));
  XOR xor_3 (.in_1(SUB), .in_2(in_1[15]), .out_3(xor_3_out_3));
  _1bit_ADDER u_1bit_adder_1 (
    .ci_1(n1bit_adder_1_ci_1), .ai(xor_2_out_3), .bi(in_2[14]), .si(out_5[14]), .ci(n1bit_adder_3_ci_1));
  _1bit_ADDER u_1bit_adder_2 (
    .ci_1(n1bit_adder_2_ci_1), .ai(xor_3_out_3), .bi(in_2[15]), .si(out_5[15]), .ci(n1bit_adder_1_ci_1));
  XOR xor_4 (.in_1(SUB), .in_2(in_1[13]), .out_3(xor_4_out_3));
  XOR xor_5 (.in_1(SUB), .in_2(in_1[12]), .out_3(xor_5_out_3));
  _1bit_ADDER u_1bit_adder_3 (
    .ci_1(n1bit_adder_3_ci_1), .ai(xor_4_out_3), .bi(in_2[13]), .si(out_5[13]), .ci(n1bit_adder_4_ci_1));
  _1bit_ADDER u_1bit_adder_4 (
    .ci_1(n1bit_adder_4_ci_1), .ai(xor_5_out_3), .bi(in_2[12]), .si(out_5[12]), .ci(n1bit_adder_5_ci_1));
  XOR xor_6 (.in_1(SUB), .in_2(in_1[10]), .out_3(xor_6_out_3));
  XOR xor_7 (.in_1(SUB), .in_2(in_1[11]), .out_3(xor_7_out_3));
  _1bit_ADDER u_1bit_adder_5 (
    .ci_1(n1bit_adder_5_ci_1), .ai(xor_7_out_3), .bi(in_2[11]), .si(out_5[11]), .ci(n1bit_adder_6_ci_1));
  _1bit_ADDER u_1bit_adder_6 (
    .ci_1(n1bit_adder_6_ci_1), .ai(xor_6_out_3), .bi(in_2[10]), .si(out_5[10]), .ci(n1bit_adder_8_ci_1));
  XOR xor_8 (.in_1(SUB), .in_2(in_1[8]), .out_3(xor_8_out_3));
  XOR xor_9 (.in_1(SUB), .in_2(in_1[9]), .out_3(xor_9_out_3));
  _1bit_ADDER u_1bit_adder_7 (
    .ci_1(n1bit_adder_7_ci_1), .ai(xor_8_out_3), .bi(in_2[8]), .si(out_5[8]), .ci(n1bit_adder_10_ci_1));
  _1bit_ADDER u_1bit_adder_8 (
    .ci_1(n1bit_adder_8_ci_1), .ai(xor_9_out_3), .bi(in_2[9]), .si(out_5[9]), .ci(n1bit_adder_7_ci_1));
  XOR xor_10 (.in_1(SUB), .in_2(in_1[7]), .out_3(xor_10_out_3));
  XOR xor_11 (.in_1(SUB), .in_2(in_1[6]), .out_3(xor_11_out_3));
  _1bit_ADDER u_1bit_adder_9 (
    .ci_1(n1bit_adder_9_ci_1), .ai(xor_11_out_3), .bi(in_2[6]), .si(out_5[6]), .ci(n1bit_adder_11_ci_1));
  _1bit_ADDER u_1bit_adder_10 (
    .ci_1(n1bit_adder_10_ci_1), .ai(xor_10_out_3), .bi(in_2[7]), .si(out_5[7]), .ci(n1bit_adder_9_ci_1));
  XOR xor_12 (.in_1(SUB), .in_2(in_1[5]), .out_3(xor_12_out_3));
  XOR xor_13 (.in_1(SUB), .in_2(in_1[4]), .out_3(xor_13_out_3));
  _1bit_ADDER u_1bit_adder_11 (
    .ci_1(n1bit_adder_11_ci_1), .ai(xor_12_out_3), .bi(in_2[5]), .si(out_5[5]), .ci(n1bit_adder_12_ci_1));
  _1bit_ADDER u_1bit_adder_12 (
    .ci_1(n1bit_adder_12_ci_1), .ai(xor_13_out_3), .bi(in_2[4]), .si(out_5[4]), .ci(n1bit_adder_14_ci_1));
  XOR xor_14 (.in_1(SUB), .in_2(in_1[2]), .out_3(xor_14_out_3));
  XOR xor_15 (.in_1(SUB), .in_2(in_1[3]), .out_3(xor_15_out_3));
  _1bit_ADDER u_1bit_adder_13 (
    .ci_1(n1bit_adder_13_ci_1), .ai(xor_14_out_3), .bi(in_2[2]), .si(out_5[2]), .ci(n1bit_adder_15_ci_1));
  _1bit_ADDER u_1bit_adder_14 (
    .ci_1(n1bit_adder_14_ci_1), .ai(xor_15_out_3), .bi(in_2[3]), .si(out_5[3]), .ci(n1bit_adder_13_ci_1));
  XOR xor_16 (.in_1(SUB), .in_2(in_1[0]), .out_3(xor_16_out_3));
  XOR xor_17 (.in_1(SUB), .in_2(in_1[1]), .out_3(xor_17_out_3));
  _1bit_ADDER u_1bit_adder_15 (
    .ci_1(n1bit_adder_15_ci_1), .ai(xor_17_out_3), .bi(in_2[1]), .si(out_5[1]), .ci(n1bit_adder_16_ci_1));
  _1bit_ADDER u_1bit_adder_16 (.ci_1(n1bit_adder_16_ci_1), .ai(xor_16_out_3), .bi(in_2[0]), .si(out_5[0]), .ci(SUB));

  // Notes on the sheet:
  //   XOR
  //   B
  //   rt
  //   rd
  //   XOR
  //   1bit-ADDER
  //   A
  //   rs
  //   0 +
  //   1 -
  //   A-B
  //   A+B
endmodule

module _4_1_MUX_16bit (
  input  [15:0] in_1,
  input  [15:0] in_2,
  input  [15:0] in_3,
  input  [15:0] in_4,
  input  [1:0] Select,
  output [15:0] out_6
);

  wire [15:0] n2_1_mux_16bit_1_out_4, n2_1_mux_16bit_2_out_4;

  _2_1_MUX_16bit u_2_1_mux_16bit_1 (.in_1(in_1), .in_2(in_2), .Select(Select[0]), .out_4(n2_1_mux_16bit_1_out_4));
  _2_1_MUX_16bit u_2_1_mux_16bit_2 (.in_1(in_3), .in_2(in_4), .Select(Select[0]), .out_4(n2_1_mux_16bit_2_out_4));
  _2_1_MUX_16bit u_2_1_mux_16bit_3 (
    .in_1(n2_1_mux_16bit_1_out_4), .in_2(n2_1_mux_16bit_2_out_4), .Select(Select[1]), .out_4(out_6));

  // Notes on the sheet:
  //   00
  //   01
  //   10
  //   11
  //   2-1 MUX
  //   2-1 MUX
  //   2-1 MUX
endmodule

module _2_1_MUX_1bit (
  input  _0,
  input  _1,
  input  S,
  output out_4
);

  wire and_1_out, and_2_out, not_1_out;

  not not_1 (not_1_out, S);
  and and_1 (and_1_out, _0, not_1_out);
  and and_2 (and_2_out, _1, S);
  or or_1 (out_4, and_1_out, and_2_out);
endmodule

module RegisterFile (
  input  [15:0] in_1,
  input  Writing_Enable,
  input  [1:0] RS,
  input  [1:0] RT,
  input  [1:0] Writing_Sel,
  output [15:0] REG0,
  output [15:0] REG1,
  output [15:0] REG2,
  output [15:0] REG3,
  output [15:0] out_10,
  output [15:0] out_11
);

  wire clock_1_out;
  wire [15:0] controlled_buffer_1_out, selection_assignment_1_4_16bit_1_out_3,
       selection_assignment_1_4_16bit_1_out_4, selection_assignment_1_4_16bit_1_out_5,
       selection_assignment_1_4_16bit_1_out_6;

  assign controlled_buffer_1_out = Writing_Enable ? in_1 : 16'bz;  // Controlled_Buffer controlled_buffer_1
  Selection_Assignment_1_4__16bit selection_assignment_1_4_16bit_1 (
    .in_1(controlled_buffer_1_out), .in_2(Writing_Sel), .out_3(selection_assignment_1_4_16bit_1_out_3),
    .out_4(selection_assignment_1_4_16bit_1_out_4), .out_5(selection_assignment_1_4_16bit_1_out_5),
    .out_6(selection_assignment_1_4_16bit_1_out_6));
  Clock #(.highDuration(1), .lowDuration(1)) clock_1 (.out(clock_1_out));
  Register #(.width(16)) register_1 (
    .D(selection_assignment_1_4_16bit_1_out_3), .Q(REG0), .clk(clock_1_out));  // open: en, clr
  Register #(.width(16)) register_2 (
    .D(selection_assignment_1_4_16bit_1_out_4), .Q(REG1), .clk(clock_1_out));  // open: en, clr
  Register #(.width(16)) register_3 (
    .D(selection_assignment_1_4_16bit_1_out_5), .Q(REG2), .clk(clock_1_out));  // open: en, clr
  Register #(.width(16)) register_4 (
    .D(selection_assignment_1_4_16bit_1_out_6), .Q(REG3), .clk(clock_1_out));  // open: en, clr
  _4_1_MUX_16bit u_4_1_mux_16bit_1 (.in_1(REG0), .in_2(REG1), .in_3(REG2), .in_4(REG3), .Select(RS), .out_6(out_10));
  _4_1_MUX_16bit u_4_1_mux_16bit_2 (.in_1(REG0), .in_2(REG1), .in_3(REG2), .in_4(REG3), .Select(RT), .out_6(out_11));

  // Notes on the sheet:
  //   Sel_Assignment 1-4
  //   00
  //   01
  //   10
  //   11
  //   4-1 MUX
  //   4-1 MUX
  //   Reading_Sel
  //   RS
  //   RT
endmodule

module _2_1_MUX_16bit (
  input  [15:0] in_1,
  input  [15:0] in_2,
  input  Select,
  output [15:0] out_4
);

  _2_1_MUX_1bit u_2_1_mux_1bit_1 (._0(in_1[0]), ._1(in_2[0]), .S(Select), .out_4(out_4[0]));
  _2_1_MUX_1bit u_2_1_mux_1bit_2 (._0(in_1[1]), ._1(in_2[1]), .S(Select), .out_4(out_4[1]));
  _2_1_MUX_1bit u_2_1_mux_1bit_3 (._0(in_1[2]), ._1(in_2[2]), .S(Select), .out_4(out_4[2]));
  _2_1_MUX_1bit u_2_1_mux_1bit_4 (._0(in_1[3]), ._1(in_2[3]), .S(Select), .out_4(out_4[3]));
  _2_1_MUX_1bit u_2_1_mux_1bit_5 (._0(in_1[4]), ._1(in_2[4]), .S(Select), .out_4(out_4[4]));
  _2_1_MUX_1bit u_2_1_mux_1bit_6 (._0(in_1[5]), ._1(in_2[5]), .S(Select), .out_4(out_4[5]));
  _2_1_MUX_1bit u_2_1_mux_1bit_7 (._0(in_1[6]), ._1(in_2[6]), .S(Select), .out_4(out_4[6]));
  _2_1_MUX_1bit u_2_1_mux_1bit_8 (._0(in_1[7]), ._1(in_2[7]), .S(Select), .out_4(out_4[7]));
  _2_1_MUX_1bit u_2_1_mux_1bit_9 (._0(in_1[8]), ._1(in_2[8]), .S(Select), .out_4(out_4[8]));
  _2_1_MUX_1bit u_2_1_mux_1bit_10 (._0(in_1[9]), ._1(in_2[9]), .S(Select), .out_4(out_4[9]));
  _2_1_MUX_1bit u_2_1_mux_1bit_11 (._0(in_1[10]), ._1(in_2[10]), .S(Select), .out_4(out_4[10]));
  _2_1_MUX_1bit u_2_1_mux_1bit_12 (._0(in_1[11]), ._1(in_2[11]), .S(Select), .out_4(out_4[11]));
  _2_1_MUX_1bit u_2_1_mux_1bit_13 (._0(in_1[12]), ._1(in_2[12]), .S(Select), .out_4(out_4[12]));
  _2_1_MUX_1bit u_2_1_mux_1bit_14 (._0(in_1[13]), ._1(in_2[13]), .S(Select), .out_4(out_4[13]));
  _2_1_MUX_1bit u_2_1_mux_1bit_15 (._0(in_1[14]), ._1(in_2[14]), .S(Select), .out_4(out_4[14]));
  _2_1_MUX_1bit u_2_1_mux_1bit_16 (._0(in_1[15]), ._1(in_2[15]), .S(Select), .out_4(out_4[15]));

  // Notes on the sheet:
  //   0
  //   1
  //   2-1 MUX(1BIT)
endmodule

module Selection_Assignment_1_4__16bit (
  input  [15:0] in_1,
  input  [1:0] in_2,
  output [15:0] out_3,
  output [15:0] out_4,
  output [15:0] out_5,
  output [15:0] out_6
);

  wire and_1_out, and_2_out, and_3_out, and_4_out, not_1_out, not_2_out, not_3_out, not_4_out;

  assign out_3 = and_1_out ? in_1 : 16'bz;  // Controlled_Buffer controlled_buffer_1
  and and_1 (and_1_out, not_1_out, not_2_out);
  not not_1 (not_1_out, in_2[1]);
  not not_2 (not_2_out, in_2[0]);
  assign out_4 = and_2_out ? in_1 : 16'bz;  // Controlled_Buffer controlled_buffer_2
  and and_2 (and_2_out, not_3_out, in_2[0]);
  not not_3 (not_3_out, in_2[1]);
  assign out_5 = and_3_out ? in_1 : 16'bz;  // Controlled_Buffer controlled_buffer_3
  and and_3 (and_3_out, in_2[1], not_4_out);
  not not_4 (not_4_out, in_2[0]);
  assign out_6 = and_4_out ? in_1 : 16'bz;  // Controlled_Buffer controlled_buffer_4
  and and_4 (and_4_out, in_2[1], in_2[0]);

  // Notes on the sheet:
  //   00
  //   01
  //   Used in RegisterFile
  //   10
  //   11
  //   00
  //   01
  //   10
  //   11
endmodule

module PC (
  input  [11:0] in_1,
  input  [7:0] Immediate_8,
  input  nPC_Sel,
  input  Whether_Jump,
  output [15:0] current_PC
);

  wire clock_1_out;
  wire [11:0] n2_1_mux_16bit_2_out_4_2;
  wire [15:0] n2_1_mux_16bit_1_out_4, n16bit_adder_1_out_5, n16bit_adder_2_out_5;
  wire [15:12] n2_1_mux_16bit_2_out_4;

  Clock #(.highDuration(1), .lowDuration(1)) clock_1 (.out(clock_1_out));
  _16bit_ADDER u_16bit_adder_1 (
    .in_1(current_PC), .in_2(16'h1), .out_5(n16bit_adder_1_out_5), .SUB(1'b0));  // open: Overflow
  _2_1_MUX_16bit u_2_1_mux_16bit_1 (
    .in_1({n2_1_mux_16bit_2_out_4, n2_1_mux_16bit_2_out_4_2}), .in_2({n2_1_mux_16bit_2_out_4, in_1}),
    .Select(Whether_Jump), .out_4(n2_1_mux_16bit_1_out_4));
  _2_1_MUX_16bit u_2_1_mux_16bit_2 (
    .in_1(n16bit_adder_1_out_5), .in_2(n16bit_adder_2_out_5), .Select(nPC_Sel),
    .out_4({n2_1_mux_16bit_2_out_4, n2_1_mux_16bit_2_out_4_2}));
  _16bit_ADDER u_16bit_adder_2 (
    .in_1(n16bit_adder_1_out_5), .in_2({{6{1'b0}}, Immediate_8, 2'b00}), .out_5(n16bit_adder_2_out_5),
    .SUB(1'b0));  // open: Overflow
  Register #(.width(16)) register_1 (.D(n2_1_mux_16bit_1_out_4), .Q(current_PC), .clk(clock_1_out));  // open: en, clr

  // Notes on the sheet:
  //   ADDER
  //   MUX
  //   +
  //   ADDER
  //   MUX
  //   +
  //   Address_for_jumping
endmodule

module _2_1_MUX_8bit (
  input  [7:0] _0,
  input  [7:0] in_2,
  input  Select,
  output [7:0] out_4
);

  _2_1_MUX_1bit u_2_1_mux_1bit_1 (._0(_0[0]), ._1(in_2[0]), .S(Select), .out_4(out_4[0]));
  _2_1_MUX_1bit u_2_1_mux_1bit_2 (._0(_0[1]), ._1(in_2[1]), .S(Select), .out_4(out_4[1]));
  _2_1_MUX_1bit u_2_1_mux_1bit_3 (._0(_0[2]), ._1(in_2[2]), .S(Select), .out_4(out_4[2]));
  _2_1_MUX_1bit u_2_1_mux_1bit_4 (._0(_0[3]), ._1(in_2[3]), .S(Select), .out_4(out_4[3]));
  _2_1_MUX_1bit u_2_1_mux_1bit_5 (._0(_0[4]), ._1(in_2[4]), .S(Select), .out_4(out_4[4]));
  _2_1_MUX_1bit u_2_1_mux_1bit_6 (._0(_0[5]), ._1(in_2[5]), .S(Select), .out_4(out_4[5]));
  _2_1_MUX_1bit u_2_1_mux_1bit_7 (._0(_0[6]), ._1(in_2[6]), .S(Select), .out_4(out_4[6]));
  _2_1_MUX_1bit u_2_1_mux_1bit_8 (._0(_0[7]), ._1(in_2[7]), .S(Select), .out_4(out_4[7]));

  // Notes on the sheet:
  //   1
  //   2-1 MUX(1BIT)
endmodule

module _8bit_ADDER (
  input  [7:0] in_1,
  input  [7:0] in_2,
  input  _0_plus,
  output Overflow,
  output [7:0] out_5
);

  wire n1bit_adder_1_ci_1, n1bit_adder_2_ci_1, n1bit_adder_3_ci_1, n1bit_adder_4_ci_1, n1bit_adder_5_ci_1,
       n1bit_adder_6_ci_1, n1bit_adder_7_ci_1, n1bit_adder_8_ci_1, xor_2_out_3, xor_3_out_3, xor_4_out_3,
       xor_5_out_3, xor_6_out_3, xor_7_out_3, xor_8_out_3, xor_9_out_3;

  XOR xor_1 (.in_1(n1bit_adder_2_ci_1), .in_2(n1bit_adder_1_ci_1), .out_3(Overflow));
  XOR xor_2 (.in_1(_0_plus), .in_2(in_1[7]), .out_3(xor_2_out_3));
  _1bit_ADDER u_1bit_adder_1 (
    .ci_1(n1bit_adder_1_ci_1), .ai(xor_2_out_3), .bi(in_2[7]), .si(out_5[7]), .ci(n1bit_adder_2_ci_1));
  XOR xor_3 (.in_1(_0_plus), .in_2(in_1[6]), .out_3(xor_3_out_3));
  XOR xor_4 (.in_1(_0_plus), .in_2(in_1[5]), .out_3(xor_4_out_3));
  _1bit_ADDER u_1bit_adder_2 (
    .ci_1(n1bit_adder_2_ci_1), .ai(xor_3_out_3), .bi(in_2[6]), .si(out_5[6]), .ci(n1bit_adder_3_ci_1));
  XOR xor_5 (.in_1(_0_plus), .in_2(in_1[4]), .out_3(xor_5_out_3));
  _1bit_ADDER u_1bit_adder_3 (
    .ci_1(n1bit_adder_3_ci_1), .ai(xor_4_out_3), .bi(in_2[5]), .si(out_5[5]), .ci(n1bit_adder_4_ci_1));
  _1bit_ADDER u_1bit_adder_4 (
    .ci_1(n1bit_adder_4_ci_1), .ai(xor_5_out_3), .bi(in_2[4]), .si(out_5[4]), .ci(n1bit_adder_5_ci_1));
  XOR xor_6 (.in_1(_0_plus), .in_2(in_1[3]), .out_3(xor_6_out_3));
  _1bit_ADDER u_1bit_adder_5 (
    .ci_1(n1bit_adder_5_ci_1), .ai(xor_6_out_3), .bi(in_2[3]), .si(out_5[3]), .ci(n1bit_adder_6_ci_1));
  XOR xor_7 (.in_1(_0_plus), .in_2(in_1[2]), .out_3(xor_7_out_3));
  _1bit_ADDER u_1bit_adder_6 (
    .ci_1(n1bit_adder_6_ci_1), .ai(xor_7_out_3), .bi(in_2[2]), .si(out_5[2]), .ci(n1bit_adder_7_ci_1));
  XOR xor_8 (.in_1(_0_plus), .in_2(in_1[1]), .out_3(xor_8_out_3));
  _1bit_ADDER u_1bit_adder_7 (
    .ci_1(n1bit_adder_7_ci_1), .ai(xor_8_out_3), .bi(in_2[1]), .si(out_5[1]), .ci(n1bit_adder_8_ci_1));
  XOR xor_9 (.in_1(_0_plus), .in_2(in_1[0]), .out_3(xor_9_out_3));
  _1bit_ADDER u_1bit_adder_8 (.ci_1(n1bit_adder_8_ci_1), .ai(xor_9_out_3), .bi(in_2[0]), .si(out_5[0]), .ci(_0_plus));

  // Notes on the sheet:
  //   XOR
  //   1bit-ADDER
  //   SUB
  //   1 -
endmodule

module Instruction_Fetch (
  input  [15:0] in_1,
  output [2:0] Funct,
  output [2:0] Party_bits,
  output [1:0] rd,
  output [1:0] rt,
  output [1:0] rs,
  output [3:0] Opcode,
  output [7:0] out_8,
  output [11:0] out_9
);


  assign Funct = in_1[15:13];
  assign in_1[2:0] = in_1[15:13];
  assign Opcode = in_1[15:12];
  assign out_8 = in_1[15:8];
  assign out_9 = {in_1[11:3], in_1[15:13]};
  assign Party_bits = in_1[5:3];
  assign rd = in_1[7:6];
  assign rs = in_1[11:10];
  assign rt = in_1[9:8];

  // Notes on the sheet:
  //   R-Format
  //   I-Format
  //   J-Format
  //   immediate
  //   address
endmodule

module Memory_Data (
  input  [15:0] in_1,
  input  [15:0] Address_Input,
  input  MemWriting,
  output [15:0] out_4
);

  wire clock_1_out, not_1_out;

  Clock #(.highDuration(1), .lowDuration(1)) clock_1 (.out(clock_1_out));
  RAM #(.addrWidth(16), .dataWidth(16)) ram_1 (
    .addr(Address_Input), .data(out_4), .clk(clock_1_out), .ld(not_1_out));  // open: sel, clr
  not not_1 (not_1_out, MemWriting);
  assign out_4 = MemWriting ? in_1 : 16'bz;  // Controlled_Buffer controlled_buffer_1

  // Notes on the sheet:
  //   Value_Writing
endmodule

module lui (
  input  [15:0] in_1,
  output [15:0] out_2
);


  assign out_2 = {in_1[7:0], {8{1'b0}}};

  // Notes on the sheet:
  //   rt
endmodule

module sllv (
  input  [15:0] in_1,
  input  [15:0] in_2,
  output [15:0] out_3
);

  wire not_1_out, or_1_out, or_2_out, or_3_out;
  wire [12:10] undriven_3;
  wire [14:11] undriven_4;
  wire [15:0] n16_1_mux_16bit_1_out_18;
  wire [15:9] undriven_2;
  wire [15:12] undriven_5;
  wire [15:13] undriven_6;
  wire [15:14] undriven_7;
  wire [15:15] undriven;

  _16_1_MUX_16bit u_16_1_mux_16bit_1 (
    .in_1(in_1), .in_2({in_1[14:0], 1'b0}), .in_3({undriven_2, in_1[15:7]}),
    .in_4({in_1[2:0], undriven_3, in_1[15:6]}), .in_5({in_1[0], undriven_4, in_1[15:5]}),
    .in_6({undriven_5, in_1[15:4]}), .in_7({undriven_6, in_1[15:3]}), .in_8({undriven_7, in_1[15:2]}),
    .in_9({undriven[15], in_1[15:1]}), .in_10(in_1), .in_11({in_1[14:0], 1'b0}), .in_12({in_1[13:0], 2'b00}),
    .in_13({in_1[12:0], 3'b000}), .in_14({in_1[11:0], 4'b0000}), .in_15({in_1[10:0], {5{1'b0}}}),
    .in_16({in_1[9:0], {6{1'b0}}}), .in_17(in_2[3:0]), .out_18(n16_1_mux_16bit_1_out_18));
  or or_1 (or_1_out, in_2[4], in_2[5], in_2[6], in_2[7], in_2[8]);
  or or_2 (or_2_out, in_2[9], in_2[10], in_2[11], in_2[12], in_2[13]);
  or or_3 (or_3_out, or_1_out, or_2_out, in_2[14], in_2[15]);
  assign out_3 = not_1_out ? n16_1_mux_16bit_1_out_18 : 16'bz;  // Controlled_Buffer controlled_buffer_1
  not not_1 (not_1_out, or_3_out);
  assign out_3 = or_3_out ? {16{1'b0}} : 16'bz;  // Controlled_Buffer controlled_buffer_2
  // also tied to GND on the sheet: {in_1[0], in_1[1], in_1[2], in_1[3], in_1[4], in_1[5], in_1[6], in_1[7], in_1[8]}

  // Notes on the sheet:
  //   Number
  //   rt
  //   rs
  //   Offset
  //   Hex
  //   Shut down when overflow
  //   And the output is zero
  //   rd
endmodule

module _8_1_MUX_16bit (
  input  [15:0] in_1,
  input  [15:0] in_2,
  input  [15:0] in_3,
  input  [15:0] in_4,
  input  [15:0] in_5,
  input  [15:0] in_6,
  input  [15:0] in_7,
  input  [15:0] in_8,
  input  [2:0] in_9,
  output [15:0] out_10
);

  wire [15:0] n2_1_mux_16bit_1_out_4, n2_1_mux_16bit_2_out_4, n2_1_mux_16bit_3_out_4, n2_1_mux_16bit_4_out_4,
       n2_1_mux_16bit_5_out_4, n2_1_mux_16bit_6_out_4;

  _2_1_MUX_16bit u_2_1_mux_16bit_1 (.in_1(in_1), .in_2(in_2), .Select(in_9[0]), .out_4(n2_1_mux_16bit_1_out_4));
  _2_1_MUX_16bit u_2_1_mux_16bit_2 (.in_1(in_3), .in_2(in_4), .Select(in_9[0]), .out_4(n2_1_mux_16bit_2_out_4));
  _2_1_MUX_16bit u_2_1_mux_16bit_3 (.in_1(in_5), .in_2(in_6), .Select(in_9[0]), .out_4(n2_1_mux_16bit_3_out_4));
  _2_1_MUX_16bit u_2_1_mux_16bit_4 (.in_1(in_7), .in_2(in_8), .Select(in_9[0]), .out_4(n2_1_mux_16bit_4_out_4));
  _2_1_MUX_16bit u_2_1_mux_16bit_5 (
    .in_1(n2_1_mux_16bit_1_out_4), .in_2(n2_1_mux_16bit_2_out_4), .Select(in_9[1]),
    .out_4(n2_1_mux_16bit_5_out_4));
  _2_1_MUX_16bit u_2_1_mux_16bit_6 (
    .in_1(n2_1_mux_16bit_3_out_4), .in_2(n2_1_mux_16bit_4_out_4), .Select(in_9[1]),
    .out_4(n2_1_mux_16bit_6_out_4));
  _2_1_MUX_16bit u_2_1_mux_16bit_7 (
    .in_1(n2_1_mux_16bit_5_out_4), .in_2(n2_1_mux_16bit_6_out_4), .Select(in_9[2]), .out_4(out_10));

  // Notes on the sheet:
  //   000
  //   001
  //   010
  //   011
  //   100
  //   101
  //   110
  //   111
endmodule

module _16_1_MUX_16bit (
  input  [15:0] in_1,
  input  [15:0] in_2,
  input  [15:0] in_3,
  input  [15:0] in_4,
  input  [15:0] in_5,
  input  [15:0] in_6,
  input  [15:0] in_7,
  input  [15:0] in_8,
  input  [15:0] in_9,
  input  [15:0] in_10,
  input  [15:0] in_11,
  input  [15:0] in_12,
  input  [15:0] in_13,
  input  [15:0] in_14,
  input  [15:0] in_15,
  input  [15:0] in_16,
  input  [3:0] in_17,
  output [15:0] out_18
);

  wire [15:0] n8_1_mux_16bit_1_out_10, n8_1_mux_16bit_2_out_10;

  _8_1_MUX_16bit u_8_1_mux_16bit_1 (
    .in_1(in_1), .in_2(in_2), .in_3(in_3), .in_4(in_4), .in_5(in_5), .in_6(in_6), .in_7(in_7), .in_8(in_8),
    .in_9(in_17[2:0]), .out_10(n8_1_mux_16bit_1_out_10));
  _8_1_MUX_16bit u_8_1_mux_16bit_2 (
    .in_1(in_9), .in_2(in_10), .in_3(in_11), .in_4(in_12), .in_5(in_13), .in_6(in_14), .in_7(in_15),
    .in_8(in_16), .in_9(in_17[2:0]), .out_10(n8_1_mux_16bit_2_out_10));
  _2_1_MUX_16bit u_2_1_mux_16bit_1 (
    .in_1(n8_1_mux_16bit_1_out_10), .in_2(n8_1_mux_16bit_2_out_10), .Select(in_17[3]), .out_4(out_18));

  // Notes on the sheet:
  //   0000
  //   0001
  //   0010
  //   0011
  //   0100
  //   0101
  //   0110
  //   0111
  //   1000
  //   1001
  //   1010
  //   1011
  //   1100
  //   1101
  //   1110
  //   1111
endmodule

module srav (
  input  [15:0] in_1,
  input  [15:0] in_2,
  output [15:0] out_3
);

  wire not_1_out, or_1_out, or_2_out, or_3_out;
  wire [1:0] undriven_2;
  wire [2:0] undriven;
  wire [15:0] n16_1_mux_16bit_1_out_18;

  _16_1_MUX_16bit u_16_1_mux_16bit_1 (
    .in_1({in_1[15:7], {7{in_1[15]}}}), .in_2({{2{in_1[15]}}, in_1[14:7], {6{in_1[15]}}}),
    .in_3({{3{in_1[15]}}, in_1[14:7], {5{in_1[15]}}}), .in_4({{4{in_1[15]}}, in_1[14:7], {4{in_1[15]}}}),
    .in_5({{5{in_1[15]}}, in_1[14:7], {3{in_1[15]}}}), .in_6({{6{in_1[15]}}, in_1[14:7], {2{in_1[15]}}}),
    .in_7({{7{in_1[15]}}, in_1[14:7], in_1[15]}), .in_8({{8{in_1[15]}}, in_1[14:7]}),
    .in_9({{9{in_1[15]}}, in_1[14:8]}), .in_10({{10{in_1[15]}}, in_1[14:9]}),
    .in_11({{11{in_1[15]}}, in_1[14:10]}), .in_12({{12{in_1[15]}}, in_1[14:11]}),
    .in_13({{13{in_1[15]}}, in_1[14:12]}), .in_14({{13{in_1[15]}}, undriven}),
    .in_15({{14{in_1[15]}}, undriven_2}), .in_16({16{in_1[15]}}), .in_17(in_2[3:0]),
    .out_18(n16_1_mux_16bit_1_out_18));
  or or_1 (or_1_out, in_2[4], in_2[5], in_2[6], in_2[7], in_2[8]);
  or or_2 (or_2_out, in_2[9], in_2[10], in_2[11], in_2[12], in_2[13]);
  or or_3 (or_3_out, or_1_out, or_2_out, in_2[14], in_2[15]);
  assign out_3 = not_1_out ? n16_1_mux_16bit_1_out_18 : 16'bz;  // Controlled_Buffer controlled_buffer_1
  not not_1 (not_1_out, or_3_out);
  assign out_3 = or_3_out ? {16{1'b0}} : 16'bz;  // Controlled_Buffer controlled_buffer_2

  assign in_1[6:0] = {7{in_1[15]}};

  // Notes on the sheet:
  //   Number
  //   rs
  //   rt
  //   Offset
  //   rd
endmodule

module slt (
  input  [15:0] in_1,
  input  [15:0] in_2,
  output [15:0] out_3
);

  wire [15:0] n16bit_adder_1_out_5;

  _16bit_ADDER u_16bit_adder_1 (.in_1(in_2), .in_2(in_1), .out_5(n16bit_adder_1_out_5), .SUB(1'b1));  // open: Overflow
  not not_1 (out_3[0], n16bit_adder_1_out_5[15]);

  assign out_3[15:1] = {15{1'b0}};

  // Notes on the sheet:
  //   a
  //   rt
  //   rs
  //   b
  //   SUB
  //   a-b
  //   0: a-b>0,1:a-b<0
endmodule

module srlv (
  input  [15:0] Number,
  input  [15:0] in_2,
  output [15:0] out_3
);

  wire not_1_out, or_1_out, or_2_out, or_3_out;
  wire [1:0] undriven_3;
  wire [2:0] undriven_2;
  wire [3:0] undriven;
  wire [5:0] undriven_4;
  wire [15:0] n16_1_mux_16bit_1_out_18;

  or or_1 (or_1_out, in_2[4], in_2[5], in_2[6], in_2[7], in_2[8]);
  or or_2 (or_2_out, in_2[9], in_2[10], in_2[11], in_2[12], in_2[13]);
  _16_1_MUX_16bit u_16_1_mux_16bit_1 (
    .in_1(Number), .in_2({1'b0, Number[15:1]}), .in_3({2'b00, Number[15:2]}), .in_4({3'b000, Number[15:3]}),
    .in_5({4'b0000, Number[15:4]}), .in_6({{5{1'b0}}, Number[15:5]}), .in_7({{6{1'b0}}, Number[15:6]}),
    .in_8({{7{1'b0}}, Number[15:7]}), .in_9({{8{1'b0}}, Number[15:8]}), .in_10({{9{1'b0}}, Number[15:9]}),
    .in_11({{10{1'b0}}, undriven_4}), .in_12({Number[7:0], 3'b000, Number[15:11]}),
    .in_13({{12{1'b0}}, undriven}), .in_14({Number[7:0], {5{1'b0}}, undriven_2}),
    .in_15({Number[7:0], {6{1'b0}}, undriven_3}), .in_16({Number[7:0], {7{1'b0}}, Number[15]}),
    .in_17(in_2[3:0]), .out_18(n16_1_mux_16bit_1_out_18));
  or or_3 (or_3_out, or_1_out, or_2_out, in_2[14], in_2[15]);
  assign out_3 = not_1_out ? n16_1_mux_16bit_1_out_18 : 16'bz;  // Controlled_Buffer controlled_buffer_1
  assign out_3 = or_3_out ? {16{1'b0}} : 16'bz;  // Controlled_Buffer controlled_buffer_2
  not not_1 (not_1_out, or_3_out);
  // also tied to GND on the sheet: {Number[0], Number[1], Number[2], Number[3], Number[4], Number[5], Number[6], Number[7]}

  // Notes on the sheet:
  //   rs
  //   rt
  //   Offset
  //   rd
endmodule

module beq (
  input  [15:0] in_1,
  input  [15:0] in_2,
  output Equal
);

  wire or_1_out, or_2_out, or_3_out, or_4_out;
  wire [15:0] n16bit_adder_1_out_5;

  _16bit_ADDER u_16bit_adder_1 (.in_1(in_2), .in_2(in_1), .out_5(n16bit_adder_1_out_5), .SUB(1'b1));  // open: Overflow
  or or_1 (or_1_out, n16bit_adder_1_out_5[0], n16bit_adder_1_out_5[1], n16bit_adder_1_out_5[2], n16bit_adder_1_out_5[3], n16bit_adder_1_out_5[4]);
  or or_2 (or_2_out, n16bit_adder_1_out_5[11], n16bit_adder_1_out_5[12], n16bit_adder_1_out_5[13], n16bit_adder_1_out_5[14], n16bit_adder_1_out_5[15]);
  or or_3 (or_3_out, n16bit_adder_1_out_5[5], n16bit_adder_1_out_5[6], n16bit_adder_1_out_5[7], n16bit_adder_1_out_5[8], n16bit_adder_1_out_5[9], n16bit_adder_1_out_5[10]);
  or or_4 (or_4_out, or_1_out, or_3_out, or_2_out);
  not not_1 (Equal, or_4_out);

  // Notes on the sheet:
  //   rs
  //   rt
  //   SUB
endmodule

module bne (
  input  [15:0] in_1,
  input  [15:0] in_2,
  output Equal
);

  wire or_1_out, or_2_out, or_3_out;
  wire [15:0] n16bit_adder_1_out_5;

  _16bit_ADDER u_16bit_adder_1 (.in_1(in_2), .in_2(in_1), .out_5(n16bit_adder_1_out_5), .SUB(1'b1));  // open: Overflow
  or or_1 (or_1_out, n16bit_adder_1_out_5[0], n16bit_adder_1_out_5[1], n16bit_adder_1_out_5[2], n16bit_adder_1_out_5[3], n16bit_adder_1_out_5[4]);
  or or_2 (or_2_out, n16bit_adder_1_out_5[11], n16bit_adder_1_out_5[12], n16bit_adder_1_out_5[13], n16bit_adder_1_out_5[14], n16bit_adder_1_out_5[15]);
  or or_3 (or_3_out, n16bit_adder_1_out_5[5], n16bit_adder_1_out_5[6], n16bit_adder_1_out_5[7], n16bit_adder_1_out_5[8], n16bit_adder_1_out_5[9], n16bit_adder_1_out_5[10]);
  or or_4 (Equal, or_1_out, or_3_out, or_2_out);

  // Notes on the sheet:
  //   rs
  //   rt
  //   SUB
endmodule

module ALU (
  input  [15:0] in_1,
  input  [15:0] in_2,
  input  [3:0] ALUclr,
  output [15:0] out_4,
  output Equal
);

  wire beq_1_equal, bne_1_equal;
  wire [15:0] and_1_out, lui_1_out_2, n16bit_adder_1_out_5, n16bit_adder_2_out_5, or_1_out, sllv_1_out_3,
       slt_1_out_3, srav_1_out_3, srlv_1_out_3;

  _16bit_ADDER u_16bit_adder_1 (.in_1(in_2), .in_2(in_1), .out_5(n16bit_adder_1_out_5), .SUB(1'b0));  // open: Overflow
  _16bit_ADDER u_16bit_adder_2 (.in_1(in_2), .in_2(in_1), .out_5(n16bit_adder_2_out_5), .SUB(1'b1));  // open: Overflow
  assign and_1_out = in_1 & in_2;  // AND_Gate and_1, 16 bits wide
  assign or_1_out = in_1 | in_2;  // OR_Gate or_1, 16 bits wide
  slt slt_1 (.in_1(in_2), .in_2(in_1), .out_3(slt_1_out_3));
  srlv srlv_1 (.in_2(in_2), .Number(in_1), .out_3(srlv_1_out_3));
  sllv sllv_1 (.in_2(in_2), .in_1(in_1), .out_3(sllv_1_out_3));
  srav srav_1 (.in_2(in_2), .in_1(in_1), .out_3(srav_1_out_3));
  lui lui_1 (.in_1(in_2), .out_2(lui_1_out_2));
  beq beq_1 (.in_1(in_1), .in_2(in_2), .Equal(beq_1_equal));
  bne bne_1 (.in_1(in_1), .in_2(in_2), .Equal(bne_1_equal));
  or or_2 (Equal, beq_1_equal, bne_1_equal);
  _16_1_MUX_16bit u_16_1_mux_16bit_1 (
    .in_1(n16bit_adder_1_out_5), .in_2(n16bit_adder_2_out_5), .in_3(and_1_out), .in_4(or_1_out),
    .in_5(slt_1_out_3), .in_6(srlv_1_out_3), .in_7(sllv_1_out_3), .in_8(srav_1_out_3), .in_9(lui_1_out_2),
    .in_17(ALUclr), .out_18(out_4));  // open: in_10, in_11, in_12, in_13, in_14, in_15, in_16

  // Notes on the sheet:
  //   rs
  //   busA
  //   rt
  //   busB
  //   ADD
  //   SUB
  //   AND
  //   OR
  //   SLT
  //   SRLV
  //   SLLV
  //   SRAV
  //   LUI
  //   BEQ
  //   BNE
  //   ADD 0000
  //   SUB 0001
  //   AND 0010
  //   OR 0011
  //   SLT 0100
  //   SRLV 0101
  //   SLLV 0110
  //   SRAV 0111
  //   LUI 1000
  //   BEQ 1001
  //   BNE 1010
endmodule

module EXTEND (
  input  [7:0] in_1,
  input  Extend,
  output [15:0] out_3
);

  _2_1_MUX_16bit u_2_1_mux_16bit_1 (
    .in_1({{8{1'b0}}, in_1}), .in_2({{9{in_1[7]}}, in_1[6:0]}), .Select(Extend), .out_4(out_3));

  // Notes on the sheet:
  //   0_Extend
  //   Sign_Extend
  //   0
  //   1
endmodule

module DATAPATH (
  input  DISP,
  input  in_2,
  input  Extend,
  input  in_4,
  input  [3:0] ALUctr,
  input  MemWR,
  input  in_7,
  input  nPC_sel,
  input  Whether_jump,
  input  RegDst,
  output [2:0] Funct,
  output [2:0] Party_bit,
  output [3:0] Opcode,
  output [7:0] DISP_3,
  output [7:0] DISP_2,
  output [7:0] DISP_1,
  output [7:0] DISP_0,
  output [15:0] REG0,
  output [15:0] REG1,
  output [15:0] REG2,
  output [15:0] REG3
);

  wire alu_1_equal, and_1_out;
  wire [1:0] instruction_fetch_1_rd, instruction_fetch_1_rs, instruction_fetch_1_rt, n2_1_mux_2bit_1_out_4;
  wire [7:0] instruction_fetch_1_out_8;
  wire [11:0] instruction_fetch_1_out_9;
  wire [15:0] alu_1_out_4, extend_1_out_3, memory_data_1_out_4, n2_1_mux_16bit_1_out_4,
       n2_1_mux_16bit_2_out_4, pc_1_current_pc, registerfile_1_out_10, registerfile_1_out_11, rom_1_data;

  ROM #(.addrWidth(16), .dataWidth(16)) rom_1 (.addr(pc_1_current_pc), .data(rom_1_data), .sel(1'b1));
  Instruction_Fetch instruction_fetch_1 (
    .in_1(rom_1_data), .Funct(Funct), .Party_bits(Party_bit), .rd(instruction_fetch_1_rd),
    .rt(instruction_fetch_1_rt), .rs(instruction_fetch_1_rs), .Opcode(Opcode),
    .out_8(instruction_fetch_1_out_8), .out_9(instruction_fetch_1_out_9));
  RegisterFile registerfile_1 (
    .in_1(n2_1_mux_16bit_2_out_4), .REG0(REG0), .REG1(REG1), .REG2(REG2), .REG3(REG3), .Writing_Enable(in_2),
    .Writing_Sel(n2_1_mux_2bit_1_out_4), .RS(instruction_fetch_1_rs), .RT(instruction_fetch_1_rt),
    .out_10(registerfile_1_out_10), .out_11(registerfile_1_out_11));
  _2_1_MUX_2bit u_2_1_mux_2bit_1 (
    .in_1(instruction_fetch_1_rt), .in_2(instruction_fetch_1_rd), .in_3(RegDst), .out_4(n2_1_mux_2bit_1_out_4));
  EXTEND extend_1 (.in_1(instruction_fetch_1_out_8), .Extend(Extend), .out_3(extend_1_out_3));
  _2_1_MUX_16bit u_2_1_mux_16bit_1 (
    .in_1(registerfile_1_out_11), .in_2(extend_1_out_3), .Select(in_4), .out_4(n2_1_mux_16bit_1_out_4));
  and and_1 (and_1_out, nPC_sel, alu_1_equal);
  ALU alu_1 (
    .in_1(registerfile_1_out_10), .in_2(n2_1_mux_16bit_1_out_4), .ALUclr(ALUctr), .out_4(alu_1_out_4),
    .Equal(alu_1_equal));
  Disp u_disp_1 (
    .Disp(DISP), .DISP_3(DISP_3), .DISP_2(DISP_2), .DISP_1(DISP_1), .DISP_0(DISP_0),
    .in_2(registerfile_1_out_10), .in_3(instruction_fetch_1_out_8));
  PC pc_1 (
    .current_PC(pc_1_current_pc), .Immediate_8(instruction_fetch_1_out_8), .in_1(instruction_fetch_1_out_9),
    .nPC_Sel(and_1_out), .Whether_Jump(Whether_jump));
  Memory_Data memory_data_1 (
    .in_1(registerfile_1_out_11), .Address_Input(alu_1_out_4), .MemWriting(MemWR), .out_4(memory_data_1_out_4));
  _2_1_MUX_16bit u_2_1_mux_16bit_2 (
    .in_1(alu_1_out_4), .in_2(memory_data_1_out_4), .Select(in_7), .out_4(n2_1_mux_16bit_2_out_4));

  // Notes on the sheet:
  //   Instruction Memory
  //   Turn it on
  //   Instruction Fetch
  //   8-immediate
  //   Result Write
  //   rd
  //   RegisterFile
  //   Writing_Enable
  //   rt
  //   RS
  //   RT
  //   RS
  //   RT
  //   ALUsrc
  //   MUX
  //   Extend
  //   address_for_jumping
  //   MUX
  //   MemToReg
  //   ALU
  //   8-immediate
  //   Equal
  //   PC
  //   Disp
  //   Data Memory
  //   MUX
endmodule

module _2_1_MUX_2bit (
  input  [1:0] in_1,
  input  [1:0] in_2,
  input  in_3,
  output [1:0] out_4
);

  wire and_1_out, and_2_out, and_3_out, and_4_out, not_1_out, not_2_out;

  not not_1 (not_1_out, in_3);
  not not_2 (not_2_out, in_3);
  and and_1 (and_1_out, in_1[1], not_1_out);
  and and_2 (and_2_out, in_2[1], in_3);
  and and_3 (and_3_out, in_1[0], not_2_out);
  and and_4 (and_4_out, in_2[0], in_3);
  or or_1 (out_4[1], and_1_out, and_2_out);
  or or_2 (out_4[0], and_3_out, and_4_out);
endmodule

module Disp (
  input  Disp,
  input  [15:0] in_2,
  input  [7:0] in_3,
  output [7:0] DISP_3,
  output [7:0] DISP_2,
  output [7:0] DISP_1,
  output [7:0] DISP_0
);

  wire and_1_out, not_1_out, or_1_out;
  wire [7:0] selection_assgnment_1_4_8bit_1_out_3, selection_assgnment_1_4_8bit_1_out_4,
       selection_assgnment_1_4_8bit_1_out_5, selection_assgnment_1_4_8bit_1_out_6;

  assign DISP_3 = and_1_out ? selection_assgnment_1_4_8bit_1_out_6 : 8'bz;  // Controlled_Buffer controlled_buffer_1
  assign DISP_2 = and_1_out ? selection_assgnment_1_4_8bit_1_out_5 : 8'bz;  // Controlled_Buffer controlled_buffer_2
  Selection_Assgnment_1_4__8bit selection_assgnment_1_4_8bit_1 (
    .in_1(in_2[7:0]), .in_2(in_3[1:0]), .out_3(selection_assgnment_1_4_8bit_1_out_3),
    .out_4(selection_assgnment_1_4_8bit_1_out_4), .out_5(selection_assgnment_1_4_8bit_1_out_5),
    .out_6(selection_assgnment_1_4_8bit_1_out_6));
  assign DISP_1 = and_1_out ? selection_assgnment_1_4_8bit_1_out_4 : 8'bz;  // Controlled_Buffer controlled_buffer_3
  not not_1 (not_1_out, or_1_out);
  and and_1 (and_1_out, not_1_out, Disp);
  or or_1 (or_1_out, in_3[7], in_3[6], in_3[5], in_3[4], in_3[3], in_3[2]);
  assign DISP_0 = and_1_out ? selection_assgnment_1_4_8bit_1_out_3 : 8'bz;  // Controlled_Buffer controlled_buffer_4

  // Notes on the sheet:
  //   Selection Assignment
  //   Rs
  //   imm
endmodule

module Selection_Assgnment_1_4__8bit (
  input  [7:0] in_1,
  input  [1:0] in_2,
  output [7:0] out_3,
  output [7:0] out_4,
  output [7:0] out_5,
  output [7:0] out_6
);

  wire and_1_out, and_2_out, and_3_out, and_4_out, not_1_out, not_2_out, not_3_out, not_4_out;

  assign out_3 = and_1_out ? in_1 : 8'bz;  // Controlled_Buffer controlled_buffer_1
  and and_1 (and_1_out, not_2_out, not_1_out);
  not not_1 (not_1_out, in_2[0]);
  not not_2 (not_2_out, in_2[1]);
  assign out_4 = and_2_out ? in_1 : 8'bz;  // Controlled_Buffer controlled_buffer_2
  and and_2 (and_2_out, not_3_out, in_2[0]);
  not not_3 (not_3_out, in_2[1]);
  assign out_5 = and_3_out ? in_1 : 8'bz;  // Controlled_Buffer controlled_buffer_3
  and and_3 (and_3_out, in_2[1], not_4_out);
  not not_4 (not_4_out, in_2[0]);
  assign out_6 = and_4_out ? in_1 : 8'bz;  // Controlled_Buffer controlled_buffer_4
  and and_4 (and_4_out, in_2[1], in_2[0]);

  // Notes on the sheet:
  //   00
  //   01
  //   Used in Disp
  //   10
  //   11
  //   00
  //   01
  //   10
  //   11
endmodule

module Control (
  input  [2:0] Funct,
  input  [3:0] Opcode,
  output RegDest,
  output Writing_Enable,
  output DISP,
  output ALUsrc,
  output [3:0] ALUctr,
  output Extend,
  output MemToReg,
  output MemWR,
  output Whether_Jump,
  output nPC_Sel
);

  wire and_1_out, and_2_out, and_3_out, and_4_out, and_5_out, and_6_out, and_7_out, and_8_out, and_10_out,
       and_11_out, and_12_out, and_13_out, and_17_out, and_18_out, not_1_out, not_2_out, not_3_out,
       not_4_out, not_5_out, not_6_out, not_7_out, not_8_out, not_9_out, not_10_out, not_11_out, not_12_out,
       not_13_out, not_14_out, not_15_out, not_16_out, not_17_out, not_18_out, not_19_out, not_20_out,
       not_21_out, not_22_out, not_23_out, not_24_out, not_25_out, not_26_out, not_27_out, not_28_out,
       not_29_out, not_30_out, not_31_out, not_32_out, not_33_out, not_34_out, not_35_out, not_36_out,
       not_37_out, not_38_out, not_39_out, not_40_out, not_41_out, not_42_out, not_43_out, not_44_out,
       not_45_out, not_46_out, not_47_out, not_48_out, not_49_out, not_50_out, not_51_out, not_52_out,
       not_53_out, not_54_out, not_55_out, not_56_out, not_57_out, not_58_out, not_59_out, not_60_out,
       not_61_out, not_62_out, not_63_out, not_64_out, not_65_out, not_66_out, not_67_out, or_1_out,
       or_2_out, or_5_out, or_9_out, or_10_out;
  wire [3:0] controlled_buffer_1_out, controlled_buffer_2_out, controlled_buffer_3_out,
       controlled_buffer_4_out, controlled_buffer_5_out, controlled_buffer_6_out, controlled_buffer_7_out,
       controlled_buffer_8_out, controlled_buffer_9_out, controlled_buffer_10_out, controlled_buffer_11_out,
       or_11_out, or_12_out;

  not not_1 (not_1_out, Funct[0]);
  not not_2 (not_2_out, Funct[1]);
  not not_3 (not_3_out, Funct[2]);
  not not_4 (not_4_out, Opcode[0]);
  not not_5 (not_5_out, Opcode[1]);
  not not_6 (not_6_out, Opcode[2]);
  not not_7 (not_7_out, Opcode[3]);
  not not_8 (not_8_out, Funct[1]);
  not not_9 (not_9_out, Funct[2]);
  not not_10 (not_10_out, Opcode[0]);
  not not_11 (not_11_out, Opcode[1]);
  not not_12 (not_12_out, Opcode[2]);
  not not_13 (not_13_out, Opcode[3]);
  not not_14 (not_14_out, Funct[0]);
  not not_15 (not_15_out, Funct[2]);
  not not_16 (not_16_out, Opcode[0]);
  not not_17 (not_17_out, Opcode[1]);
  not not_18 (not_18_out, Opcode[2]);
  not not_19 (not_19_out, Opcode[3]);
  not not_20 (not_20_out, Funct[2]);
  not not_21 (not_21_out, Opcode[0]);
  not not_22 (not_22_out, Opcode[1]);
  not not_23 (not_23_out, Opcode[2]);
  not not_24 (not_24_out, Opcode[3]);
  not not_25 (not_25_out, Funct[0]);
  not not_26 (not_26_out, Funct[1]);
  not not_27 (not_27_out, Opcode[0]);
  not not_28 (not_28_out, Opcode[1]);
  not not_29 (not_29_out, Opcode[2]);
  not not_30 (not_30_out, Opcode[3]);
  not not_31 (not_31_out, Funct[1]);
  not not_32 (not_32_out, Opcode[0]);
  not not_33 (not_33_out, Opcode[1]);
  not not_34 (not_34_out, Opcode[2]);
  not not_35 (not_35_out, Opcode[3]);
  not not_36 (not_36_out, Funct[0]);
  not not_37 (not_37_out, Opcode[0]);
  not not_38 (not_38_out, Opcode[1]);
  not not_39 (not_39_out, Opcode[2]);
  not not_40 (not_40_out, Opcode[3]);
  not not_41 (not_41_out, Opcode[0]);
  not not_42 (not_42_out, Opcode[1]);
  not not_43 (not_43_out, Opcode[2]);
  not not_44 (not_44_out, Opcode[3]);
  not not_45 (not_45_out, Opcode[1]);
  not not_46 (not_46_out, Opcode[2]);
  not not_47 (not_47_out, Opcode[3]);
  not not_48 (not_48_out, Opcode[0]);
  not not_49 (not_49_out, Opcode[2]);
  not not_50 (not_50_out, Opcode[3]);
  not not_51 (not_51_out, Opcode[2]);
  not not_52 (not_52_out, Opcode[3]);
  not not_53 (not_53_out, Opcode[0]);
  not not_54 (not_54_out, Opcode[1]);
  not not_55 (not_55_out, Opcode[3]);
  not not_56 (not_56_out, Opcode[1]);
  not not_57 (not_57_out, Opcode[3]);
  not not_58 (not_58_out, Opcode[0]);
  not not_59 (not_59_out, Opcode[3]);
  not not_60 (not_60_out, Opcode[3]);
  not not_61 (not_61_out, Opcode[0]);
  not not_62 (not_62_out, Opcode[1]);
  not not_63 (not_63_out, Opcode[2]);
  not not_64 (not_64_out, Opcode[1]);
  not not_65 (not_65_out, Opcode[2]);
  not not_66 (not_66_out, Opcode[0]);
  not not_67 (not_67_out, Opcode[2]);
  and and_1 (and_1_out, not_1_out, not_2_out, not_3_out, not_4_out, not_5_out, not_6_out, not_7_out);
  and and_2 (and_2_out, Funct[0], not_8_out, not_9_out, not_10_out, not_11_out, not_12_out, not_13_out);
  and and_3 (and_3_out, not_14_out, Funct[1], not_15_out, not_16_out, not_17_out, not_18_out, not_19_out);
  and and_4 (and_4_out, Funct[0], Funct[1], not_20_out, not_21_out, not_22_out, not_23_out, not_24_out);
  and and_5 (and_5_out, not_25_out, not_26_out, Funct[2], not_27_out, not_28_out, not_29_out, not_30_out);
  and and_6 (and_6_out, Funct[0], not_31_out, Funct[2], not_32_out, not_33_out, not_34_out, not_35_out);
  and and_7 (and_7_out, not_36_out, Funct[1], Funct[2], not_37_out, not_38_out, not_39_out, not_40_out);
  and and_8 (and_8_out, Funct[0], Funct[1], Funct[2], not_41_out, not_42_out, not_43_out, not_44_out);
  and and_9 (DISP, Opcode[0], not_45_out, not_46_out, not_47_out);
  and and_10 (and_10_out, not_48_out, Opcode[1], not_49_out, not_50_out);
  and and_11 (and_11_out, Opcode[0], Opcode[1], not_51_out, not_52_out);
  and and_12 (and_12_out, not_53_out, not_54_out, Opcode[2], not_55_out);
  and and_13 (and_13_out, Opcode[0], not_56_out, Opcode[2], not_57_out);
  and and_14 (MemToReg, not_58_out, Opcode[1], Opcode[2], not_59_out);
  and and_15 (MemWR, Opcode[0], Opcode[1], Opcode[2], not_60_out);
  and and_16 (Whether_Jump, not_61_out, not_62_out, not_63_out, Opcode[3]);
  and and_17 (and_17_out, Opcode[0], not_64_out, not_65_out, Opcode[3]);
  and and_18 (and_18_out, not_66_out, Opcode[1], not_67_out, Opcode[3]);
  or or_1 (or_1_out, and_1_out, and_2_out, and_3_out, and_4_out, and_5_out, and_6_out, and_7_out);
  or or_2 (or_2_out, and_8_out, and_10_out, and_11_out, and_12_out, and_13_out, MemToReg);
  or or_3 (RegDest, and_1_out, and_2_out, and_3_out, and_4_out, and_5_out, and_6_out, and_7_out, and_8_out);
  or or_4 (Writing_Enable, or_1_out, or_2_out);
  or or_5 (or_5_out, and_2_out, and_13_out);
  or or_6 (ALUsrc, DISP, and_10_out, and_11_out, and_12_out, and_13_out, MemToReg, MemWR);
  or or_7 (Extend, and_12_out, MemToReg, MemWR);
  or or_8 (nPC_Sel, and_17_out, and_18_out);
  or or_9 (or_9_out, and_3_out, MemWR, and_12_out, MemToReg);
  or or_10 (or_10_out, and_1_out, and_11_out);
  assign controlled_buffer_1_out = and_18_out ? 4'b1010 : 4'bz;  // Controlled_Buffer controlled_buffer_1
  assign controlled_buffer_2_out = and_17_out ? 4'b1001 : 4'bz;  // Controlled_Buffer controlled_buffer_2
  assign controlled_buffer_3_out = and_10_out ? 4'b1000 : 4'bz;  // Controlled_Buffer controlled_buffer_3
  assign controlled_buffer_4_out = and_7_out ? 4'b0111 : 4'bz;  // Controlled_Buffer controlled_buffer_4
  assign controlled_buffer_5_out = and_5_out ? 4'b0110 : 4'bz;  // Controlled_Buffer controlled_buffer_5
  assign controlled_buffer_6_out = and_6_out ? 4'b0101 : 4'bz;  // Controlled_Buffer controlled_buffer_6
  assign controlled_buffer_7_out = and_8_out ? 4'b0100 : 4'bz;  // Controlled_Buffer controlled_buffer_7
  assign or_11_out = controlled_buffer_7_out | controlled_buffer_8_out | controlled_buffer_9_out | controlled_buffer_10_out | controlled_buffer_11_out;  // OR_Gate or_11, 4 bits wide
  assign or_12_out = controlled_buffer_2_out | controlled_buffer_3_out | controlled_buffer_4_out | controlled_buffer_5_out | controlled_buffer_6_out;  // OR_Gate or_12, 4 bits wide
  assign ALUctr = controlled_buffer_1_out | or_12_out | or_11_out;  // OR_Gate or_13, 4 bits wide
  assign controlled_buffer_8_out = or_10_out ? 4'b0011 : 4'bz;  // Controlled_Buffer controlled_buffer_8
  assign controlled_buffer_9_out = or_5_out ? 4'b0010 : 4'bz;  // Controlled_Buffer controlled_buffer_9
  assign controlled_buffer_10_out = and_4_out ? 4'b0001 : 4'bz;  // Controlled_Buffer controlled_buffer_10
  assign controlled_buffer_11_out = or_9_out ? 4'b0000 : 4'bz;  // Controlled_Buffer controlled_buffer_11

  // Notes on the sheet:
  //   OR
  //   AND
  //   ADD
  //   SUB
  //   SLLV
  //   SRLV
  //   SRAV
  //   SLT
  //   DISP
  //   LUI
  //   ORI
  //   ADDI
  //   ANDI
  //   LW
  //   SW
  //   JUMP
  //   BEQ
  //   BNE
  //   BNE
  //   LUI
  //   BEQ
  //   SRAV
  //   SLLV
  //   SRLV
  //   SLT
  //   AND
  //   OR
  //   ADD
  //   SUB
endmodule

module BlockBottom (
  input  [7:0] in_1,
  input  [7:0] in_2,
  input  [7:0] in_3,
  input  [7:0] in_4,
  output out_5,
  output out_6,
  output out_7,
  output out_8,
  output out_9,
  output out_10,
  output out_11,
  output out_12,
  output out_13,
  output out_14,
  output out_15,
  output out_16,
  output out_17,
  output out_18,
  output out_19,
  output out_20
);

  ConverterBottom converterbottom_1 (.in_1(in_1), .out_2(out_13), .out_3(out_5), .out_4(out_6), .out_5(out_14));
  ConverterBottom converterbottom_2 (.in_1(in_2), .out_2(out_15), .out_3(out_7), .out_4(out_8), .out_5(out_16));
  ConverterBottom converterbottom_3 (.in_1(in_3), .out_2(out_17), .out_3(out_9), .out_4(out_10), .out_5(out_18));
  ConverterBottom converterbottom_4 (.in_1(in_4), .out_2(out_19), .out_3(out_11), .out_4(out_12), .out_5(out_20));
endmodule

module BlockTop (
  input  [7:0] in_1,
  input  [7:0] in_2,
  input  [7:0] in_3,
  input  [7:0] in_4,
  output out_5,
  output out_6,
  output out_7,
  output out_8,
  output out_9,
  output out_10,
  output out_11,
  output out_12,
  output out_13,
  output out_14,
  output out_15,
  output out_16,
  output out_17,
  output out_18,
  output out_19,
  output out_20
);

  ConverterTop convertertop_1 (.in_1(in_1), .out_2(out_5), .out_3(out_13), .out_4(out_14), .out_5(out_6));
  ConverterTop convertertop_2 (.in_1(in_2), .out_2(out_7), .out_3(out_15), .out_4(out_16), .out_5(out_8));
  ConverterTop convertertop_3 (.in_1(in_3), .out_2(out_9), .out_3(out_17), .out_4(out_18), .out_5(out_10));
  ConverterTop convertertop_4 (.in_1(in_4), .out_2(out_11), .out_3(out_19), .out_4(out_20), .out_5(out_12));
endmodule

module blackbox (
  input  [7:0] in_1,
  input  [7:0] in_2,
  input  [7:0] in_3,
  input  [7:0] in_4,
  output [7:0] out_5,
  output [7:0] out_6,
  output [7:0] out_7,
  output [7:0] out_8
);


  assign out_5 = in_1;
  assign out_6 = in_2;
  assign out_7 = in_3;
  assign out_8 = in_4;
endmodule

module ConverterBottom (
  input  [7:0] in_1,
  output out_2,
  output out_3,
  output out_4,
  output out_5
);

  wire and_1_out, or_1_out;
  wire [3:0] multiplexer_3_out;
  wire [7:0] multiplexer_1_out, multiplexer_2_out;

  Multiplexer #(.select(4), .width(8)) multiplexer_1 (
    .in0(8'h77), .in1(8'h41), .in2(8'h3b), .in3(8'h6b), .in4(8'h4d), .in5(8'h6e), .in6(8'h7e), .in7(8'h43),
    .in8(8'h7f), .in9(8'h6f), .in10(8'h5f), .in11(8'h7c), .in12(8'h36), .in13(8'h79), .in14(8'h3e),
    .in15(8'h1e), .out(multiplexer_1_out), .sel(in_1[3:0]));
  or or_1 (or_1_out, in_1[4], in_1[5], in_1[6], in_1[7]);
  Multiplexer #(.select(1), .width(8)) multiplexer_2 (
    .in0(multiplexer_1_out), .in1(8'h9b), .out(multiplexer_2_out), .sel(or_1_out));
  and and_1 (and_1_out, in_1[0], in_1[1], in_1[2], in_1[3], in_1[4], in_1[5], in_1[6], in_1[7]);
  Multiplexer #(.select(1), .width(8)) multiplexer_3 (
    .in0(multiplexer_2_out), .in1({8{1'b0}}), .out({out_5, out_4, out_3, out_2, multiplexer_3_out}),
    .sel(and_1_out));

  // Notes on the sheet:
  //   0
  //   1
  //   2
  //   3
  //   4
  //   5
  //   6
  //   7
  //   8
  //   9
  //   a
  //   b
  //   c
  //   d
  //   e
  //   f
  //   ?
endmodule

module ConverterTop (
  input  [7:0] in_1,
  output out_2,
  output out_3,
  output out_4,
  output out_5
);

  wire and_1_out, or_1_out;
  wire [7:0] multiplexer_1_out, multiplexer_2_out;
  wire [7:4] multiplexer_3_out;

  Multiplexer #(.select(4), .width(8)) multiplexer_1 (
    .in0(8'h77), .in1(8'h41), .in2(8'h3b), .in3(8'h6b), .in4(8'h4d), .in5(8'h6e), .in6(8'h7e), .in7(8'h43),
    .in8(8'h7f), .in9(8'h6f), .in10(8'h5f), .in11(8'h7c), .in12(8'h36), .in13(8'h79), .in14(8'h3e),
    .in15(8'h1e), .out(multiplexer_1_out), .sel(in_1[3:0]));
  or or_1 (or_1_out, in_1[4], in_1[5], in_1[6], in_1[7]);
  Multiplexer #(.select(1), .width(8)) multiplexer_2 (
    .in0(multiplexer_1_out), .in1(8'h9b), .out(multiplexer_2_out), .sel(or_1_out));
  and and_1 (and_1_out, in_1[0], in_1[1], in_1[2], in_1[3], in_1[4], in_1[5], in_1[6], in_1[7]);
  Multiplexer #(.select(1), .width(8)) multiplexer_3 (
    .in0(multiplexer_2_out), .in1({8{1'b0}}), .out({multiplexer_3_out, out_2, out_3, out_4, out_5}),
    .sel(and_1_out));

  // Notes on the sheet:
  //   0
  //   1
  //   2
  //   3
  //   4
  //   5
  //   6
  //   7
  //   8
  //   9
  //   a
  //   b
  //   c
  //   d
  //   e
  //   f
  //   ?
endmodule

module Converter (
  input  [7:0] in_1,
  output out_2,
  output out_3,
  output out_4,
  output out_5,
  output out_6,
  output out_7,
  output out_8,
  output out_9
);

  wire and_1_out, or_1_out;
  wire [7:0] multiplexer_1_out, multiplexer_2_out;

  Multiplexer #(.select(4), .width(8)) multiplexer_1 (
    .in0(8'h77), .in1(8'h41), .in2(8'h3b), .in3(8'h6b), .in4(8'h4d), .in5(8'h6e), .in6(8'h7e), .in7(8'h43),
    .in8(8'h7f), .in9(8'h6f), .in10(8'h5f), .in11(8'h7c), .in12(8'h36), .in13(8'h79), .in14(8'h3e),
    .in15(8'h1e), .out(multiplexer_1_out), .sel(in_1[3:0]));
  or or_1 (or_1_out, in_1[4], in_1[5], in_1[6], in_1[7]);
  Multiplexer #(.select(1), .width(8)) multiplexer_2 (
    .in0(multiplexer_1_out), .in1(8'h9b), .out(multiplexer_2_out), .sel(or_1_out));
  and and_1 (and_1_out, in_1[0], in_1[1], in_1[2], in_1[3], in_1[4], in_1[5], in_1[6], in_1[7]);
  Multiplexer #(.select(1), .width(8)) multiplexer_3 (
    .in0(multiplexer_2_out), .in1({8{1'b0}}), .out({out_9, out_8, out_7, out_6, out_2, out_3, out_4, out_5}),
    .sel(and_1_out));

  // Notes on the sheet:
  //   0
  //   1
  //   2
  //   3
  //   4
  //   5
  //   6
  //   7
  //   8
  //   9
  //   a
  //   b
  //   c
  //   d
  //   e
  //   f
  //   ?
endmodule

module Examples (
  input  [7:0] in_1,
  input  [7:0] in_2,
  input  [7:0] in_3,
  input  [7:0] in_4,
  input  [7:0] in_5
);

  wire blockbottom_1_out_5, blockbottom_1_out_6, blockbottom_1_out_7, blockbottom_1_out_8,
       blockbottom_1_out_9, blockbottom_1_out_10, blockbottom_1_out_11, blockbottom_1_out_12,
       blockbottom_1_out_13, blockbottom_1_out_14, blockbottom_1_out_15, blockbottom_1_out_16,
       blockbottom_1_out_17, blockbottom_1_out_18, blockbottom_1_out_19, blockbottom_1_out_20,
       blocktop_1_out_5, blocktop_1_out_6, blocktop_1_out_7, blocktop_1_out_8, blocktop_1_out_9,
       blocktop_1_out_10, blocktop_1_out_11, blocktop_1_out_12, blocktop_1_out_13, blocktop_1_out_14,
       blocktop_1_out_15, blocktop_1_out_16, blocktop_1_out_17, blocktop_1_out_18, blocktop_1_out_19,
       blocktop_1_out_20, converterbottom_1_out_2, converterbottom_1_out_3, converterbottom_1_out_4,
       converterbottom_1_out_5, convertertop_1_out_2, convertertop_1_out_3, convertertop_1_out_4,
       convertertop_1_out_5;
  wire [7:0] blackbox_1_out_5, blackbox_1_out_6, blackbox_1_out_7, blackbox_1_out_8;

  ConverterTop convertertop_1 (
    .in_1(in_1), .out_2(convertertop_1_out_2), .out_3(convertertop_1_out_3), .out_4(convertertop_1_out_4),
    .out_5(convertertop_1_out_5));
  _7_Segment_Display u_7_segment_display_1 (
    .g(convertertop_1_out_2), .f(convertertop_1_out_3), .a(convertertop_1_out_4), .b(convertertop_1_out_5),
    .e(converterbottom_1_out_2), .d(converterbottom_1_out_3), .c(converterbottom_1_out_4),
    .dp(converterbottom_1_out_5));
  ConverterBottom converterbottom_1 (
    .in_1(in_1), .out_2(converterbottom_1_out_2), .out_3(converterbottom_1_out_3),
    .out_4(converterbottom_1_out_4), .out_5(converterbottom_1_out_5));
  _7_Segment_Display u_7_segment_display_2 (
    .g(blocktop_1_out_5), .f(blocktop_1_out_13), .a(blocktop_1_out_14), .b(blocktop_1_out_6),
    .e(blockbottom_1_out_13), .d(blockbottom_1_out_5), .c(blockbottom_1_out_6), .dp(blockbottom_1_out_14));
  BlockBottom blockbottom_1 (
    .out_13(blockbottom_1_out_13), .out_5(blockbottom_1_out_5), .out_6(blockbottom_1_out_6),
    .out_14(blockbottom_1_out_14), .out_15(blockbottom_1_out_15), .out_7(blockbottom_1_out_7),
    .out_8(blockbottom_1_out_8), .out_16(blockbottom_1_out_16), .out_17(blockbottom_1_out_17),
    .out_9(blockbottom_1_out_9), .out_10(blockbottom_1_out_10), .out_18(blockbottom_1_out_18),
    .out_19(blockbottom_1_out_19), .out_11(blockbottom_1_out_11), .out_12(blockbottom_1_out_12),
    .out_20(blockbottom_1_out_20), .in_1(blackbox_1_out_5), .in_2(blackbox_1_out_6), .in_3(blackbox_1_out_7),
    .in_4(blackbox_1_out_8));
  BlockTop blocktop_1 (
    .in_1(blackbox_1_out_5), .in_2(blackbox_1_out_6), .in_3(blackbox_1_out_7), .in_4(blackbox_1_out_8),
    .out_5(blocktop_1_out_5), .out_13(blocktop_1_out_13), .out_14(blocktop_1_out_14),
    .out_6(blocktop_1_out_6), .out_7(blocktop_1_out_7), .out_15(blocktop_1_out_15),
    .out_16(blocktop_1_out_16), .out_8(blocktop_1_out_8), .out_9(blocktop_1_out_9),
    .out_17(blocktop_1_out_17), .out_18(blocktop_1_out_18), .out_10(blocktop_1_out_10),
    .out_11(blocktop_1_out_11), .out_19(blocktop_1_out_19), .out_20(blocktop_1_out_20),
    .out_12(blocktop_1_out_12));
  _7_Segment_Display u_7_segment_display_3 (
    .g(blocktop_1_out_9), .f(blocktop_1_out_17), .a(blocktop_1_out_18), .b(blocktop_1_out_10),
    .e(blockbottom_1_out_17), .d(blockbottom_1_out_9), .c(blockbottom_1_out_10), .dp(blockbottom_1_out_18));
  _7_Segment_Display u_7_segment_display_4 (
    .g(blocktop_1_out_7), .f(blocktop_1_out_15), .a(blocktop_1_out_16), .b(blocktop_1_out_8),
    .e(blockbottom_1_out_15), .d(blockbottom_1_out_7), .c(blockbottom_1_out_8), .dp(blockbottom_1_out_16));
  blackbox blackbox_1 (
    .out_5(blackbox_1_out_5), .out_6(blackbox_1_out_6), .out_7(blackbox_1_out_7), .out_8(blackbox_1_out_8),
    .in_1(in_2), .in_2(in_3), .in_3(in_4), .in_4(in_5));
  _7_Segment_Display u_7_segment_display_5 (
    .g(blocktop_1_out_11), .f(blocktop_1_out_19), .a(blocktop_1_out_20), .b(blocktop_1_out_12),
    .e(blockbottom_1_out_19), .d(blockbottom_1_out_11), .c(blockbottom_1_out_12), .dp(blockbottom_1_out_20));

  // Notes on the sheet:
  //   ConverterTop
  //   DISP[3]
  //   DISP[1]
  //   DISP[2]
  //   DISP[2]
  //   DISP[0]
  //   Your Display Logic
  //   BlockTop
  //   BlockBottom
endmodule
